# Fritzing sketch LED-Uhr-II (saved by Fritzing 0.9.9b)

parts:
  WeMos_D1_Mini1 = WeMos D1 Mini
  NeoPixel = 12 NeoPixel Ring [part_number="Ring 12 LED"]
  NeoPixel_2 = NeoPixel Stick [part_number="Ring 32"]  # not connected
  S2 = Pushbutton [part_number=Taster package="[THT]"]
  Fototransistor_PNP = LTR-301 [part_number="PT 204-6C EVL" package=ltr-301]
  S1 = Pushbutton [package="[THT]"]
  S3 = Pushbutton [package="[THT]"]
  NeoPixel_3 = NeoPixel Stick [part_number="Ring 60"]
  R5 = Resistor [tolerance=±5% power=0.25W resistance=15k package=THT]
  R3 = Resistor [tolerance=±5% power=0.25W resistance=15k package=THT]  # not connected
  R1 = Resistor [tolerance=±5% power=0.25W resistance=15k package=THT]  # not connected
  R2 = Resistor [tolerance=±5% power=0.25W resistance=15k package=THT]  # not connected

nets:
  5V: WeMos_D1_Mini1.5V, NeoPixel.VDD
  N1: WeMos_D1_Mini1.A0, Fototransistor_PNP.C, R5.Pin_1
  N2: WeMos_D1_Mini1.D0, S3.Pin_2
  N3: WeMos_D1_Mini1.D5, NeoPixel_3.DATAIN
  N4: WeMos_D1_Mini1.D6, S1.Pin_1, S1.Pin_2
  N5: WeMos_D1_Mini1.D7, S2.Pin_1, S2.Pin_2
  N6: WeMos_D1_Mini1.G, R5.Pin_0

notes:
  LED-Uhr
  mit NeoPixel-Ringe, Taster, Fototransistor.
  12K Ohms 5%
  12K

custom parts:
  12 NeoPixel Ring: 12 ultra bright smart LED NeoPixels are arranged in a circle with 1.5" (37mm) outer diameter. The rings are 'chainable' - connect the output pin of one to the input pin of another. Use only one microcontroller pin to control as many as you can chain together! Each LED is addressable as the driver chip is inside the LED. Each one has ~18mA constant current drive so the color will be very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
  NeoPixel Stick: Make your own little LED strip arrangement with this stick of NeoPixel LEDs. We crammed 8 of the tiny 5050 (5mm x 5mm) smart RGB LEDs onto a PCB with mounting holes and a chainable design. Use only one microcontroller pin to control as many as you can chain together! Each LED is addressable as the driver chip is inside the LED. Each one has ~18mA constant current drive so the color will be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
